# Fritzing sketch Dawson-Arduino-Uno-Schematic (saved by Fritzing 0.9.10b)
breadboards: 1

parts:
  Uno_R3 = Arduino Uno (Rev3)
  Temperature_Sensor = MLX90614 [package=to-39]
  Radio_Module = XBEE-1 [package=xbee-silk]

nets:
  N1: Uno_R3.A4/SDA, Temperature_Sensor.PWM_SDA
  N2: Uno_R3.A5/SCL, Temperature_Sensor.SCL_VZ
  GND: Uno_R3.GND, Temperature_Sensor.VSS, Radio_Module.GND
  N3: Uno_R3.D0/RX, Radio_Module.DOUT
  N4: Uno_R3.D1/TX, Radio_Module.DIN
  VDD: Uno_R3.5V, Temperature_Sensor.VDD, Radio_Module.VDD
