# Fritzing sketch Dawson-Raspberry-Pi-Schematic (saved by Fritzing 0.9.10b)
breadboards: 1

parts:
  U1 = XBEE-1 [package=xbee-silk]
  Raspberry_Pi_1 = Raspberry Pi 3 [part_number=RPI-3-V1.2]

nets:
  VDD: U1.VDD, Raspberry_Pi_1.3v3
  N1: U1.DOUT, Raspberry_Pi_1.GIPO15
  N2: U1.DIN, Raspberry_Pi_1.GIPO14
  GND: U1.GND, Raspberry_Pi_1.GND
